// Logisim project ALU + ROM + RAM y Teclado  v3.circ as structural Verilog: 1 circuit, main circuit main
module main (
  input  [2:0] Opcode,
  input  Almacenar,
  input  [2:0] Opcode_2,
  output [7:0] out_4,
  output [7:0] out_5
);

  wire _0_2_out, _0_out, _1_2_out, _1_out, _2_2_out, _2_out, _3_2_out, _3_out, _4_2_out, _4_out, _5_2_out,
       _5_out, _6_2_out, _6_out, _7_2_out, _7_out, _8_2_out, _8_out, _9_2_out, _9_out, adder_1_out,
       AND_2_out, AND_3_out, AND_out, Clock_out, comparator_1_eq, Contador_2_q, Contador_q, NOT_2_out,
       NOT_3_out, NOT_4_out, NOT_7_out, not_8_out, Not_9_out, Not_10_out, NOT_out, priority_encoder_1_gs,
       priority_encoder_2_gs;
  wire [1:0] counter_1_q;
  wire [3:0] Contador_3_q, Contador_4_q, demultiplexer_1_out0, demultiplexer_1_out1, demultiplexer_2_out0,
       demultiplexer_2_out1, priority_encoder_1_out, priority_encoder_2_out, Registro_A_2_q, Registro_A_q,
       Registro_B_2_q, Registro_B_q;
  wire [7:0] adder_2_out, adder_3_out, AND_4_out, AND_5_out, bit_extender_1_out, bit_extender_2_out,
       bit_extender_3_out, bit_extender_4_out, divider_1_out, divider_2_out, multiplexer_1_out,
       multiplexer_2_out, multiplexer_3_out, multiplexer_4_out, multiplier_1_out, multiplier_2_out,
       NOT_5_out, NOT_6_out, OR_2_out, OR_out, register_1_q, rom_1_data, rom_2_data, subtractor_1_out,
       subtractor_2_out, XOR_2_out, XOR_out;

  Button _2 (.out(_2_out));
  Button _1 (.out(_1_out));
  Button _4 (.out(_4_out));
  Button _5 (.out(_5_out));
  Button _7 (.out(_7_out));
  Button _8 (.out(_8_out));
  Button _0 (.out(_0_out));
  Button _1_2 (.out(_1_2_out));
  Button _2_2 (.out(_2_2_out));
  Button _5_2 (.out(_5_2_out));
  Button _4_2 (.out(_4_2_out));
  Button _7_2 (.out(_7_2_out));
  Button _8_2 (.out(_8_2_out));
  Button _0_2 (.out(_0_2_out));
  Button _3 (.out(_3_out));
  Button _6 (.out(_6_out));
  Button _9 (.out(_9_out));
  Button _3_2 (.out(_3_2_out));
  Button _6_2 (.out(_6_2_out));
  Button _9_2 (.out(_9_2_out));
  Priority_Encoder #(.select(4)) priority_encoder_1 (
    .in0(_0_out), .in1(_1_out), .in2(_2_out), .in3(_3_out), .in4(_4_out), .in5(_5_out), .in6(_6_out),
    .in7(_7_out), .in8(_8_out), .in9(_9_out), .out(priority_encoder_1_out), .gs(priority_encoder_1_gs));  // open: in10, in11, in12, in13, in14, in15, en_out, en_in
  Priority_Encoder #(.select(4)) priority_encoder_2 (
    .in0(_0_2_out), .in1(_1_2_out), .in2(_2_2_out), .in3(_3_2_out), .in4(_4_2_out), .in5(_5_2_out),
    .in6(_6_2_out), .in7(_7_2_out), .in8(_8_2_out), .in9(_9_2_out), .out(priority_encoder_2_out),
    .gs(priority_encoder_2_gs));  // open: in10, in11, in12, in13, in14, in15, en_out, en_in
  Demultiplexer #(.width(4)) demultiplexer_1 (
    .out0(demultiplexer_1_out0), .out1(demultiplexer_1_out1), .in(priority_encoder_1_out), .sel(Contador_q));  // open: en
  Counter #(.width(1), .max('h1)) Contador (
    .Q(Contador_q), .clk(priority_encoder_1_gs));  // open: load, D, count, carry, clr
  not NOT (NOT_out, Contador_q);
  Demultiplexer #(.width(4)) demultiplexer_2 (
    .out0(demultiplexer_2_out0), .out1(demultiplexer_2_out1), .in(priority_encoder_2_out), .sel(Contador_2_q));  // open: en
  Counter #(.width(1), .max('h1)) Contador_2 (
    .Q(Contador_2_q), .clk(priority_encoder_2_gs));  // open: load, D, count, carry, clr
  and AND (AND_out, NOT_2_out, NOT_3_out);
  not NOT_2 (NOT_2_out, Contador_2_q);
  not NOT_3 (NOT_3_out, Contador_2_q);
  Register #(.width(4)) Registro_A (.D(demultiplexer_1_out0), .Q(Registro_A_q), .clk(Contador_q));  // open: en, clr
  Register #(.width(4)) Registro_B (.D(demultiplexer_1_out1), .Q(Registro_B_q), .clk(NOT_out));  // open: en, clr
  Register #(.width(4)) Registro_A_2 (
    .D(demultiplexer_2_out0), .Q(Registro_A_2_q), .clk(Contador_2_q));  // open: en, clr
  Register #(.width(4)) Registro_B_2 (.D(demultiplexer_2_out1), .Q(Registro_B_2_q), .clk(NOT_2_out));  // open: en, clr
  assign bit_extender_1_out = {{4{1'b0}}, Registro_A_q};  // Bit_Extender bit_extender_1
  assign bit_extender_2_out = {{4{1'b0}}, Registro_B_q};  // Bit_Extender bit_extender_2
  assign bit_extender_3_out = {{4{1'b0}}, Registro_A_2_q};  // Bit_Extender bit_extender_3
  assign bit_extender_4_out = {{4{1'b0}}, Registro_B_2_q};  // Bit_Extender bit_extender_4
  not NOT_4 (NOT_4_out, priority_encoder_2_gs);
  and AND_2 (AND_2_out, priority_encoder_1_gs, not_8_out);
  and AND_3 (AND_3_out, NOT_4_out, AND_out);
  Adder #(.width(1)) adder_1 (.a(AND_2_out), .b(1'b0), .out(adder_1_out), .cin(1'b1));  // open: cout
  Adder adder_2 (.a(bit_extender_1_out), .b(bit_extender_2_out), .out(adder_2_out));  // open: cin, cout
  Subtractor subtractor_1 (.a(bit_extender_1_out), .b(bit_extender_2_out), .out(subtractor_1_out));  // open: bin, bout
  Multiplier multiplier_1 (.a(bit_extender_1_out), .b(bit_extender_2_out), .out(multiplier_1_out));  // open: cin, cout
  Divider divider_1 (.a(bit_extender_1_out), .b(bit_extender_2_out), .out(divider_1_out));  // open: upper, rem
  assign NOT_5_out = ~bit_extender_1_out;  // NOT_Gate NOT_5, 8 bits wide
  assign OR_out = bit_extender_1_out | bit_extender_2_out;  // OR_Gate OR, 8 bits wide
  assign XOR_out = bit_extender_1_out ^ bit_extender_2_out;  // XOR_Gate XOR, 8 bits wide
  assign AND_4_out = bit_extender_1_out & bit_extender_2_out;  // AND_Gate AND_4, 8 bits wide
  Adder adder_3 (.a(bit_extender_3_out), .b(bit_extender_4_out), .out(adder_3_out));  // open: cin, cout
  Subtractor subtractor_2 (.a(bit_extender_3_out), .b(bit_extender_4_out), .out(subtractor_2_out));  // open: bin, bout
  Multiplier multiplier_2 (.a(bit_extender_3_out), .b(bit_extender_4_out), .out(multiplier_2_out));  // open: cin, cout
  Divider divider_2 (.a(bit_extender_3_out), .b(bit_extender_4_out), .out(divider_2_out));  // open: upper, rem
  assign OR_2_out = bit_extender_3_out | bit_extender_4_out;  // OR_Gate OR_2, 8 bits wide
  assign XOR_2_out = bit_extender_3_out ^ bit_extender_4_out;  // XOR_Gate XOR_2, 8 bits wide
  assign AND_5_out = bit_extender_3_out & bit_extender_4_out;  // AND_Gate AND_5, 8 bits wide
  assign NOT_6_out = ~bit_extender_3_out;  // NOT_Gate NOT_6, 8 bits wide
  Counter #(.width(4), .max('hf)) Contador_3 (.Q(Contador_3_q), .clk(adder_1_out));  // open: load, D, count, carry, clr
  Counter #(.width(4), .max('hf)) Contador_4 (.Q(Contador_4_q), .clk(AND_3_out));  // open: load, D, count, carry, clr
  Multiplexer #(.select(3), .width(8)) multiplexer_1 (
    .in0(adder_2_out), .in1(subtractor_1_out), .in2(multiplier_1_out), .in3(divider_1_out), .in4(OR_out),
    .in5(XOR_out), .in6(AND_4_out), .in7(NOT_5_out), .out(multiplexer_1_out), .sel(Opcode));  // open: en
  Counter #(.width(2), .max('h3)) counter_1 (.Q(counter_1_q), .clk(AND_2_out));  // open: load, D, count, carry, clr
  Multiplexer #(.select(3), .width(8)) multiplexer_2 (
    .in0(adder_3_out), .in1(subtractor_2_out), .in2(multiplier_2_out), .in3(divider_2_out), .in4(OR_2_out),
    .in5(XOR_2_out), .in6(AND_5_out), .in7(NOT_6_out), .out(multiplexer_2_out), .sel(Opcode_2));  // open: en
  not NOT_7 (NOT_7_out, AND_3_out);
  Multiplexer #(.width(8)) multiplexer_3 (
    .in0(bit_extender_1_out), .in1(bit_extender_2_out), .out(multiplexer_3_out), .sel(not_8_out));  // open: en
  not not_8 (not_8_out, Contador_q);
  Register register_1 (.D(multiplexer_1_out), .Q(register_1_q), .clk(comparator_1_eq));  // open: en, clr
  Comparator #(.width(2)) comparator_1 (.a(counter_1_q), .b(2'b11), .eq(comparator_1_eq));  // open: gt, lt
  assign out_5 = NOT_7_out ? multiplexer_2_out : 8'bz;  // Controlled_Buffer Control_de_Buffer
  Multiplexer #(.select(2), .width(8)) multiplexer_4 (
    .in0(multiplexer_3_out), .in1(multiplexer_3_out), .in2(multiplexer_3_out), .in3(register_1_q),
    .out(multiplexer_4_out), .sel(counter_1_q), .en(Almacenar));
  assign out_4 = Almacenar ? multiplexer_4_out : 8'bz;  // Controlled_Buffer Control_de_Buffer_2
  ROM #(.addrWidth(4)) rom_1 (.addr(Contador_4_q), .data(rom_1_data));  // open: sel
  ROM #(.addrWidth(4)) rom_2 (.addr(Contador_3_q), .data(rom_2_data));  // open: sel
  not Not_9 (Not_9_out, NOT_7_out);
  Clock Clock (.out(Clock_out));
  RAM ram_1 (.addr(rom_1_data), .data(out_5), .clk(AND_3_out), .ld(Not_9_out));  // open: sel, clr
  // Probe on out_4
  RAM ram_2 (.addr(rom_2_data), .data(out_4), .clk(Clock_out), .ld(Not_10_out));  // open: sel, clr
  not Not_10 (Not_10_out, Almacenar);

  // Notes on the sheet:
  //   Telcado con Push Button
  //   Franklin Leon
  //   Telcado con Push Button
  //   Franklin Leon (3-754-720)
  //   Diego Herrera (8-1019-400)
  //   Codificador de Prioridad
  //   Codificador de Prioridad
  //   Bit Extender
  //   Bit Extender
  //   Bit Extender
  //   Bit Extender
  //   ROM / Selector de la RAM
  //   ROM / Selector de la RAM
  //   Cargar Datos Almacenados
  //   contents of rom_1 (hex, n*v repeats v):
  //   0 1 2 3 4 5 6 7 8 9 a b c d e f
  //   Cargar Datos Almacenados
  //   contents of rom_2 (hex, n*v repeats v):
  //   0 1 2 3 4 5 6 7 8 9 a b c d e f
  //   RAM
  //   RAM
endmodule
