// Logisim project ALU_Circuito.circ as structural Verilog: 1 circuit, main circuit main
module main (
  input  [7:0] A_in,
  input  [7:0] B_in,
  input  [2:0] Opcode,
  output [7:0] Output
);

  wire [7:0] adder_1_out, and_1_out, divider_1_out, multiplier_1_out, not_1_out, or_1_out, subtractor_1_out,
       xor_1_out;

  assign not_1_out = ~A_in;  // NOT_Gate not_1, 8 bits wide
  Adder adder_1 (.a(A_in), .b(B_in), .out(adder_1_out));  // open: cin, cout
  Subtractor subtractor_1 (.a(A_in), .b(B_in), .out(subtractor_1_out));  // open: bin, bout
  Multiplier multiplier_1 (.a(A_in), .b(B_in), .out(multiplier_1_out));  // open: cin, cout
  Divider divider_1 (.a(A_in), .b(B_in), .out(divider_1_out));  // open: upper, rem
  assign or_1_out = A_in | B_in;  // OR_Gate or_1, 8 bits wide
  assign and_1_out = A_in & B_in;  // AND_Gate and_1, 8 bits wide
  assign xor_1_out = A_in ^ B_in;  // XOR_Gate xor_1, 8 bits wide
  Multiplexer #(.select(3), .width(8)) multiplexer_1 (
    .in0(adder_1_out), .in1(subtractor_1_out), .in2(multiplier_1_out), .in3(divider_1_out), .in4(or_1_out),
    .in5(and_1_out), .in6(xor_1_out), .in7(not_1_out), .out(Output), .sel(Opcode));  // open: en

  // Notes on the sheet:
  //   ALU
  //   + 000
  //   - 001
  //   x 010
  //   / 011
endmodule
