// Logisim project AU_Circuito.circ as structural Verilog: 1 circuit, main circuit main
module main (
  input  [7:0] A_in,
  input  [7:0] B_in,
  input  [2:0] Opcode,
  output [7:0] Output
);

  wire [7:0] adder_1_out, divider_1_out, multiplier_1_out, subtractor_1_out;

  Adder adder_1 (.a(A_in), .b(B_in), .out(adder_1_out));  // open: cin, cout
  Subtractor subtractor_1 (.a(A_in), .b(B_in), .out(subtractor_1_out));  // open: bin, bout
  Multiplier multiplier_1 (.a(A_in), .b(B_in), .out(multiplier_1_out));  // open: cin, cout
  Divider divider_1 (.a(A_in), .b(B_in), .out(divider_1_out));  // open: upper, rem
  Multiplexer #(.select(3), .width(8)) multiplexer_1 (
    .in0(adder_1_out), .in1(subtractor_1_out), .in2(multiplier_1_out), .in3(divider_1_out), .out(Output),
    .sel(Opcode));  // open: in4, in5, in6, in7, en

  // Notes on the sheet:
  //   AU
  //   + 000
  //   - 001
  //   x 010
  //   / 011
endmodule
