// Logisim project Calculadora_ROM.circ as structural Verilog: 1 circuit, main circuit main
module main (
  output [3:0] Output
);

  wire clock_1_out;
  wire [3:0] adder_1_out, counter_1_q, divider_1_out, multiplier_1_out, register_1_q, subtractor_1_out;
  wire [15:0] rom_1_data;

  Clock clock_1 (.out(clock_1_out));
  Counter #(.width(4), .max('hf)) counter_1 (
    .D(register_1_q), .Q(counter_1_q), .clr(clock_1_out));  // open: load, count, carry, clk
  Register #(.width(4)) register_1 (.Q(register_1_q), .clr(clock_1_out));  // open: D, en, clk
  ROM #(.addrWidth(4), .dataWidth(16)) rom_1 (.addr(counter_1_q), .data(rom_1_data));  // open: sel
  Adder #(.width(4)) adder_1 (.a(rom_1_data[3:0]), .b(rom_1_data[7:4]), .out(adder_1_out));  // open: cin, cout
  Subtractor #(.width(4)) subtractor_1 (
    .a(rom_1_data[3:0]), .b(rom_1_data[7:4]), .out(subtractor_1_out));  // open: bin, bout
  Multiplier #(.width(4)) multiplier_1 (
    .a(rom_1_data[3:0]), .b(rom_1_data[7:4]), .out(multiplier_1_out));  // open: cin, cout
  Divider #(.width(4)) divider_1 (.a(rom_1_data[3:0]), .b(rom_1_data[7:4]), .out(divider_1_out));  // open: upper, rem
  Multiplexer #(.select(4), .width(4)) multiplexer_1 (
    .in0(adder_1_out), .in1(subtractor_1_out), .in2(multiplier_1_out), .in3(divider_1_out), .out(Output),
    .sel(rom_1_data[11:8]));  // open: in4, in5, in6, in7, in8, in9, in10, in11, in12, in13, in14, in15, en

  // Notes on the sheet:
  //   + 00
  //   - 01
  //   x 10
  //   / 11
endmodule
