// Logisim project Calculadora_CON_ROM_RAM.circ as structural Verilog: 1 circuit, main circuit main
module main (
  input  [3:0] Selector_Para_la_Ram,
  input  Almacenar,
  output [3:0] Cargar_Datos_Almacenados,
  output [3:0] Output
);

  wire clock_1_out, clock_2_out, not_2_out;
  wire [3:0] adder_1_out, AND_out, counter_1_q, divider_1_out, multiplier_1_out, NOT_out, OR_out,
       register_1_q, subtractor_1_out, XOR_out;
  wire [15:0] rom_1_data;

  Counter #(.width(4), .max('hf)) counter_1 (.Q(counter_1_q), .clk(clock_1_out));  // open: load, D, count, carry, clr
  Register #(.width(4)) register_1 (.D(counter_1_q), .Q(register_1_q), .clk(clock_1_out));  // open: en, clr
  Clock #(.highDuration(2), .lowDuration(2)) clock_1 (.out(clock_1_out));
  ROM #(.addrWidth(4), .dataWidth(16)) rom_1 (.addr(register_1_q), .data(rom_1_data));  // open: sel
  Adder #(.width(4)) adder_1 (
    .a(rom_1_data[15:12]), .b(rom_1_data[11:8]), .out(adder_1_out), .cin(1'b0));  // open: cout
  Subtractor #(.width(4)) subtractor_1 (
    .a(rom_1_data[15:12]), .b(rom_1_data[11:8]), .out(subtractor_1_out), .bin(1'b0));  // open: bout
  Multiplier #(.width(4)) multiplier_1 (
    .a(rom_1_data[15:12]), .b(rom_1_data[11:8]), .out(multiplier_1_out), .cin(4'b0000));  // open: cout
  Divider #(.width(4)) divider_1 (
    .a(rom_1_data[15:12]), .b(rom_1_data[11:8]), .out(divider_1_out), .upper(4'b0000));  // open: rem
  assign OR_out = rom_1_data[15:12] | rom_1_data[11:8];  // OR_Gate OR, 4 bits wide
  assign AND_out = rom_1_data[15:12] & rom_1_data[11:8];  // AND_Gate AND, 4 bits wide
  assign XOR_out = rom_1_data[15:12] ^ rom_1_data[11:8];  // XOR_Gate XOR, 4 bits wide
  assign NOT_out = ~rom_1_data[15:12];  // NOT_Gate NOT, 4 bits wide
  Multiplexer #(.select(3), .width(4)) multiplexer_1 (
    .in0(adder_1_out), .in1(subtractor_1_out), .in2(multiplier_1_out), .in3(divider_1_out), .in4(OR_out),
    .in5(AND_out), .in6(XOR_out), .in7(NOT_out), .out(Output), .sel(rom_1_data[6:4]));  // open: en
  Clock #(.highDuration(2), .lowDuration(2)) clock_2 (.out(clock_2_out));
  assign Cargar_Datos_Almacenados = Almacenar ? Output : 4'bz;  // Controlled_Buffer controlled_buffer_1
  not not_2 (not_2_out, Almacenar);
  RAM #(.addrWidth(4), .dataWidth(4)) ram_1 (
    .addr(Selector_Para_la_Ram), .data(Cargar_Datos_Almacenados), .clk(clock_2_out), .ld(not_2_out));  // open: sel, clr

  // Notes on the sheet:
  //   Counter
  //   Register
  //   Clock
  //   Franklin Leon 
  //   ROM (4-16)
  //   contents of rom_1 (hex, n*v repeats v):
  //   2410 3120 2323 1420 4220
  //   Splitter (16-4)
  //   MUX (3-4)
  //   opcode
  //   Clock
  //   Datos Almacenados
  //   Control 
endmodule
