// Logisim project Teclado + ROM + RAM.circ as structural Verilog: 1 circuit, main circuit main
module main (
  input  Almacenar,
  output [3:0] Output,
  output [3:0] out_3
);

  wire _0_out, _1_out, _2_out, _3_out, _4_out, _5_out, _6_out, _7_out, _8_out, _9_out, Clock_out, Contador_q,
       Not_2_out, NOT_out, priority_encoder_1_gs;
  wire [3:0] Contador_2_q, demultiplexer_1_out0, demultiplexer_1_out1, priority_encoder_1_out, Registro_A_q,
       Registro_B_q, rom_1_data;

  Button _1 (.out(_1_out));
  Button _2 (.out(_2_out));
  Button _5 (.out(_5_out));
  Button _4 (.out(_4_out));
  Button _8 (.out(_8_out));
  Button _7 (.out(_7_out));
  Button _0 (.out(_0_out));
  Button _3 (.out(_3_out));
  Button _6 (.out(_6_out));
  Button _9 (.out(_9_out));
  Priority_Encoder #(.select(4)) priority_encoder_1 (
    .in0(_0_out), .in1(_1_out), .in2(_2_out), .in3(_3_out), .in4(_4_out), .in5(_5_out), .in6(_6_out),
    .in7(_7_out), .in8(_8_out), .in9(_9_out), .out(priority_encoder_1_out), .gs(priority_encoder_1_gs));  // open: in10, in11, in12, in13, in14, in15, en_out, en_in
  Demultiplexer #(.width(4)) demultiplexer_1 (
    .out0(demultiplexer_1_out0), .out1(demultiplexer_1_out1), .in(priority_encoder_1_out), .sel(Contador_q));  // open: en
  Counter #(.width(1), .max('h1)) Contador (
    .Q(Contador_q), .clk(priority_encoder_1_gs));  // open: load, D, count, carry, clr
  not NOT (NOT_out, Contador_q);
  Register #(.width(4)) Registro_A (.D(demultiplexer_1_out0), .Q(Registro_A_q), .clk(Contador_q));  // open: en, clr
  Register #(.width(4)) Registro_B (.D(demultiplexer_1_out1), .Q(Registro_B_q), .clk(NOT_out));  // open: en, clr
  Multiplexer #(.width(4)) multiplexer_1 (
    .in0(Registro_A_q), .in1(Registro_B_q), .out(Output), .sel(Contador_q));  // open: en
  Counter #(.width(4), .max('hf)) Contador_2 (
    .Q(Contador_2_q), .clk(priority_encoder_1_gs));  // open: load, D, count, carry, clr
  assign out_3 = Almacenar ? Output : 4'bz;  // Controlled_Buffer Control_de_Buffer
  ROM #(.addrWidth(4), .dataWidth(4)) rom_1 (.addr(Contador_2_q), .data(rom_1_data));  // open: sel
  Clock Clock (.out(Clock_out));
  RAM #(.addrWidth(4), .dataWidth(4)) ram_1 (
    .addr(rom_1_data), .data(out_3), .clk(Clock_out), .ld(Not_2_out));  // open: sel, clr
  not Not_2 (Not_2_out, Almacenar);

  // Notes on the sheet:
  //   Telcado con Push Button
  //   Franklin Leon
  //   Codificador de Prioridad
  //   Multplexor
  //   ROM / Selector de la RAM
  //   Cargar Datos Almacenados
  //   contents of rom_1 (hex, n*v repeats v):
  //   0 8 1 9 2 a 3 b 4 c 5 d 6 e 7 f
  //   RAM
endmodule
