// Logisim project ALU + ROM + RAM y Teclado.circ as structural Verilog: 1 circuit, main circuit main
module main (
  input  [2:0] Opcode,
  output [7:0] out_2
);

  wire _0_out, _1_out, _2_out, _3_out, _4_out, _5_out, _6_out, _7_out, _8_out, _9_out, AND_2_out, AND_out,
       Contador_q, NOT_2_out, NOT_3_out, NOT_5_out, Not_6_out, NOT_out, priority_encoder_1_gs;
  wire [3:0] Contador_2_q, demultiplexer_1_out0, demultiplexer_1_out1, priority_encoder_1_out, Registro_A_q,
       Registro_B_q;
  wire [7:0] adder_1_out, AND_3_out, bit_extender_1_out, bit_extender_2_out, divider_1_out,
       multiplexer_1_out, multiplier_1_out, NOT_4_out, OR_out, rom_1_data, subtractor_1_out, XOR_out;

  Button _1 (.out(_1_out));
  Button _2 (.out(_2_out));
  Button _5 (.out(_5_out));
  Button _4 (.out(_4_out));
  Button _7 (.out(_7_out));
  Button _8 (.out(_8_out));
  Button _0 (.out(_0_out));
  Button _3 (.out(_3_out));
  Button _6 (.out(_6_out));
  Button _9 (.out(_9_out));
  Priority_Encoder #(.select(4)) priority_encoder_1 (
    .in0(_0_out), .in1(_1_out), .in2(_2_out), .in3(_3_out), .in4(_4_out), .in5(_5_out), .in6(_6_out),
    .in7(_7_out), .in8(_8_out), .in9(_9_out), .out(priority_encoder_1_out), .gs(priority_encoder_1_gs));  // open: in10, in11, in12, in13, in14, in15, en_out, en_in
  Demultiplexer #(.width(4)) demultiplexer_1 (
    .out0(demultiplexer_1_out0), .out1(demultiplexer_1_out1), .in(priority_encoder_1_out), .sel(Contador_q));  // open: en
  Counter #(.width(1), .max('h1)) Contador (
    .Q(Contador_q), .clk(priority_encoder_1_gs));  // open: load, D, count, carry, clr
  not NOT (NOT_out, Contador_q);
  not NOT_2 (NOT_2_out, Contador_q);
  and AND (AND_out, NOT_out, NOT_2_out);
  Register #(.width(4)) Registro_A (.D(demultiplexer_1_out0), .Q(Registro_A_q), .clk(Contador_q));  // open: en, clr
  Register #(.width(4)) Registro_B (.D(demultiplexer_1_out1), .Q(Registro_B_q), .clk(NOT_out));  // open: en, clr
  not NOT_3 (NOT_3_out, priority_encoder_1_gs);
  assign bit_extender_1_out = {{4{1'b0}}, Registro_A_q};  // Bit_Extender bit_extender_1
  assign bit_extender_2_out = {{4{1'b0}}, Registro_B_q};  // Bit_Extender bit_extender_2
  and AND_2 (AND_2_out, NOT_3_out, AND_out);
  Adder adder_1 (.a(bit_extender_1_out), .b(bit_extender_2_out), .out(adder_1_out));  // open: cin, cout
  Subtractor subtractor_1 (.a(bit_extender_1_out), .b(bit_extender_2_out), .out(subtractor_1_out));  // open: bin, bout
  Multiplier multiplier_1 (.a(bit_extender_1_out), .b(bit_extender_2_out), .out(multiplier_1_out));  // open: cin, cout
  Divider divider_1 (.a(bit_extender_1_out), .b(bit_extender_2_out), .out(divider_1_out));  // open: upper, rem
  assign NOT_4_out = ~bit_extender_1_out;  // NOT_Gate NOT_4, 8 bits wide
  assign OR_out = bit_extender_1_out | bit_extender_2_out;  // OR_Gate OR, 8 bits wide
  assign XOR_out = bit_extender_1_out ^ bit_extender_2_out;  // XOR_Gate XOR, 8 bits wide
  assign AND_3_out = bit_extender_1_out & bit_extender_2_out;  // AND_Gate AND_3, 8 bits wide
  Counter #(.width(4), .max('hf)) Contador_2 (.Q(Contador_2_q), .clk(AND_2_out));  // open: load, D, count, carry, clr
  Multiplexer #(.select(3), .width(8)) multiplexer_1 (
    .in0(adder_1_out), .in1(subtractor_1_out), .in2(multiplier_1_out), .in3(divider_1_out), .in4(OR_out),
    .in5(XOR_out), .in6(AND_3_out), .in7(NOT_4_out), .out(multiplexer_1_out), .sel(Opcode));  // open: en
  not NOT_5 (NOT_5_out, AND_2_out);
  assign out_2 = NOT_5_out ? multiplexer_1_out : 8'bz;  // Controlled_Buffer Control_de_Buffer
  ROM #(.addrWidth(4)) rom_1 (.addr(Contador_2_q), .data(rom_1_data));  // open: sel
  not Not_6 (Not_6_out, NOT_5_out);
  RAM ram_1 (.addr(rom_1_data), .data(out_2), .clk(AND_2_out), .ld(Not_6_out));  // open: sel, clr

  // Notes on the sheet:
  //   Telcado con Push Button
  //   Codificador de Prioridad
  //   Bit Extender
  //   Bit Extender
  //   ROM / Selector de la RAM
  //   Cargar Datos Almacenados
  //   contents of rom_1 (hex, n*v repeats v):
  //   0 1 2 3 4 5 6 7 8 9 a b c d e f
  //   RAM
endmodule
