// Logisim project Complemento A2 y Multiplicar usando Adder.circ as structural Verilog: 1 circuit, main circuit main
module main (
  input  Opcode,
  output [7:0] out_2
);

  wire _0_out, _1_out, _2_out, _3_out, _4_out, _5_out, _6_out, _7_out, _8_out, _9_out, AND_2_out, AND_out,
       Contador_q, NOT_2_out, NOT_3_out, NOT_5_out, Not_6_out, NOT_out, priority_encoder_1_gs;
  wire [0:0] adder_2_out_2, adder_3_out_2;
  wire [2:0] AND_17_out;
  wire [3:0] adder_2_out, adder_3_out, adder_4_out, AND_6_out, AND_10_out, AND_14_out, Contador_2_q,
       demultiplexer_1_out0, demultiplexer_1_out1, priority_encoder_1_out, Registro_A_q, Registro_B_q;
  wire [7:0] adder_1_out, AND_18_out, bit_extender_1_out, bit_extender_2_out, multiplexer_1_out, not_4_out,
       rom_1_data;

  Button _1 (.out(_1_out));
  Button _4 (.out(_4_out));
  Button _7 (.out(_7_out));
  Button _3 (.out(_3_out));
  Button _2 (.out(_2_out));
  Button _6 (.out(_6_out));
  Button _5 (.out(_5_out));
  Button _9 (.out(_9_out));
  Button _8 (.out(_8_out));
  Button _0 (.out(_0_out));
  Priority_Encoder #(.select(4)) priority_encoder_1 (
    .in0(_0_out), .in1(_1_out), .in2(_2_out), .in3(_3_out), .in4(_4_out), .in5(_5_out), .in6(_6_out),
    .in7(_7_out), .in8(_8_out), .in9(_9_out), .out(priority_encoder_1_out), .gs(priority_encoder_1_gs));  // open: in10, in11, in12, in13, in14, in15, en_out, en_in
  Counter #(.width(1), .max('h1)) Contador (
    .Q(Contador_q), .clk(priority_encoder_1_gs));  // open: load, D, count, carry, clr
  Demultiplexer #(.width(4)) demultiplexer_1 (
    .out0(demultiplexer_1_out0), .out1(demultiplexer_1_out1), .in(priority_encoder_1_out), .sel(Contador_q));  // open: en
  not NOT (NOT_out, Contador_q);
  not NOT_2 (NOT_2_out, Contador_q);
  and AND (AND_out, NOT_out, NOT_2_out);
  and AND_2 (AND_2_out, AND_out, NOT_3_out);
  Register #(.width(4)) Registro_A (.D(demultiplexer_1_out0), .Q(Registro_A_q), .clk(Contador_q));  // open: en, clr
  Register #(.width(4)) Registro_B (.D(demultiplexer_1_out1), .Q(Registro_B_q), .clk(NOT_out));  // open: en, clr
  not NOT_3 (NOT_3_out, priority_encoder_1_gs);
  assign bit_extender_1_out = {{4{1'b0}}, Registro_A_q};  // Bit_Extender bit_extender_1
  assign bit_extender_2_out = {{4{1'b0}}, Registro_B_q};  // Bit_Extender bit_extender_2
  and AND_3 (AND_6_out[3], Registro_B_q[3], Registro_A_q[3]);
  assign not_4_out = ~bit_extender_2_out;  // NOT_Gate not_4, 8 bits wide
  and AND_4 (AND_6_out[2], Registro_B_q[3], Registro_A_q[2]);
  Adder adder_1 (.a(bit_extender_1_out), .b(not_4_out), .out(adder_1_out), .cin(1'b1));  // open: cout
  and AND_5 (AND_6_out[1], Registro_B_q[3], Registro_A_q[1]);
  and AND_6 (AND_6_out[0], Registro_B_q[3], Registro_A_q[0]);
  and AND_7 (AND_10_out[3], Registro_B_q[2], Registro_A_q[3]);
  and AND_8 (AND_10_out[2], Registro_B_q[2], Registro_A_q[2]);
  and AND_9 (AND_10_out[1], Registro_B_q[2], Registro_A_q[1]);
  and AND_10 (AND_10_out[0], Registro_B_q[2], Registro_A_q[0]);
  and AND_11 (AND_14_out[3], Registro_B_q[1], Registro_A_q[3]);
  and AND_12 (AND_14_out[2], Registro_B_q[1], Registro_A_q[2]);
  and AND_13 (AND_14_out[1], Registro_B_q[1], Registro_A_q[1]);
  and AND_14 (AND_14_out[0], Registro_B_q[1], Registro_A_q[0]);
  and AND_15 (AND_17_out[2], Registro_B_q[0], Registro_A_q[3]);
  and AND_16 (AND_17_out[1], Registro_B_q[0], Registro_A_q[2]);
  and AND_17 (AND_17_out[0], Registro_B_q[0], Registro_A_q[1]);
  Adder #(.width(4)) adder_2 (
    .a({1'b0, AND_17_out}), .b(AND_14_out), .out({adder_2_out[2:0], adder_2_out_2[0]}), .cin(1'b0),
    .cout(adder_2_out[3]));
  Adder #(.width(4)) adder_3 (
    .a(adder_2_out), .b(AND_10_out), .out({adder_3_out[2:0], adder_3_out_2[0]}), .cin(1'b0),
    .cout(adder_3_out[3]));
  and AND_18 (AND_18_out[0], Registro_B_q[0], Registro_A_q[0]);
  Adder #(.width(4)) adder_4 (.a(adder_3_out), .b(AND_6_out), .out(adder_4_out), .cin(1'b0), .cout(AND_18_out[7]));
  Multiplexer #(.width(8)) multiplexer_1 (
    .in0(adder_1_out), .in1({AND_18_out[7], adder_4_out, adder_3_out_2[0], adder_2_out_2[0], AND_18_out[0]}),
    .out(multiplexer_1_out), .sel(Opcode));  // open: en
  Counter #(.width(4), .max('hf)) Contador_2 (.Q(Contador_2_q), .clk(AND_2_out));  // open: load, D, count, carry, clr
  not NOT_5 (NOT_5_out, AND_2_out);
  assign out_2 = NOT_5_out ? multiplexer_1_out : 8'bz;  // Controlled_Buffer Control_de_Buffer
  ROM #(.addrWidth(4)) rom_1 (.addr(Contador_2_q), .data(rom_1_data));  // open: sel
  RAM ram_1 (.addr(rom_1_data), .data(out_2), .clk(AND_2_out), .ld(Not_6_out));  // open: sel, clr
  not Not_6 (Not_6_out, NOT_5_out);

  // Notes on the sheet:
  //   Telcado con Push Button
  //   Integrantes
  //   Franklin Leon
  //   Codificador de Prioridad
  //   Complemento A2
  //   Registro A: contiene el minuendo (el número del cual se va a restar).  
  //   Registro B: contiene el sustraendo (el número que se va a restar).
  //   Multiplicacion Usando Adders
  //   Opcode
  //   0 = Complemento A2
  //   1 = Multiplicar con Adders
  //   ROM / Selector de la RAM
  //   Cargar Datos Almacenados
  //   contents of rom_1 (hex, n*v repeats v):
  //   0 1 2 3 4 5 6 7 8 9 a b c d e f
  //   RAM
endmodule
