// Logisim project ALU + ROM + RAM y Teclado.circ as structural Verilog: 2 circuits, main circuit main
module main (
  output [7:0] out_1
);

  wire _0_out, _1_out, _2_out, _3_out, _4_out, _5_out, _6_out, _7_out, _8_out, _9_out, clock_1_out,
       comparator_1_eq, Contador_q, display_1_a1, display_1_b2, display_1_c2, display_1_d2, display_1_e,
       display_1_f, display_1_g, display_2_a1, display_2_b2, display_2_c2, display_2_d2, display_2_e,
       display_2_f, display_2_g, display_3_a1, display_3_b2, display_3_c2, display_3_d2, display_3_e,
       display_3_f, display_3_g, multiplexer_1_out, not_1_out, NOT_2_out, NOT_5_out, Not_6_out,
       priority_encoder_1_gs, Rest_out;
  wire [1:0] counter_1_q;
  wire [2:0] AND_16_out;
  wire [3:0] adder_3_out, adder_4_out, AND_5_out, AND_9_out, AND_13_out, bit_extender_3_out,
       bit_extender_4_out, bit_extender_5_out, Contador_2_q, demultiplexer_1_out0, demultiplexer_1_out1,
       priority_encoder_1_out, Registro_A_q, Registro_B_q, rom_1_data, subtractor_2_out;
  wire [7:0] adder_1_out, adder_2_out, AND_3_out, AND_17_out, bit_extender_1_out, bit_extender_2_out,
       divider_1_out, multiplexer_2_out, not_3_out, NOT_4_out, OR_out, subtractor_1_out, XOR_out;
  wire [11:0] rom_2_data;
  wire [15:4] rom_1_data_2;

  Button _1 (.out(_1_out));
  Button _4 (.out(_4_out));
  Button _7 (.out(_7_out));
  Button _2 (.out(_2_out));
  Button _3 (.out(_3_out));
  Button _6 (.out(_6_out));
  Button _5 (.out(_5_out));
  Button _9 (.out(_9_out));
  Button _8 (.out(_8_out));
  Button _0 (.out(_0_out));
  Button Rest (.out(Rest_out));
  Counter #(.width(2), .max('h2)) counter_1 (
    .Q(counter_1_q), .clk(priority_encoder_1_gs), .clr(Rest_out));  // open: load, D, count, carry
  Priority_Encoder #(.select(4)) priority_encoder_1 (
    .in0(_0_out), .in1(_1_out), .in2(_2_out), .in3(_3_out), .in4(_4_out), .in5(_5_out), .in6(_6_out),
    .in7(_7_out), .in8(_8_out), .in9(_9_out), .out(priority_encoder_1_out), .gs(priority_encoder_1_gs),
    .en_in(not_1_out));  // open: in10, in11, in12, in13, in14, in15, en_out
  not not_1 (not_1_out, comparator_1_eq);
  Comparator #(.width(2)) comparator_1 (.a(counter_1_q), .b(2'b10), .eq(comparator_1_eq));  // open: gt, lt
  Clock clock_1 (.out(clock_1_out));
  Counter #(.width(1), .max('h1)) Contador (
    .Q(Contador_q), .clk(priority_encoder_1_gs));  // open: load, D, count, carry, clr
  Multiplexer multiplexer_1 (
    .in0(priority_encoder_1_gs), .in1(clock_1_out), .out(multiplexer_1_out), .sel(comparator_1_eq));  // open: en
  Demultiplexer #(.width(4)) demultiplexer_1 (
    .out0(demultiplexer_1_out0), .out1(demultiplexer_1_out1), .in(priority_encoder_1_out), .sel(Contador_q));  // open: en
  not NOT_2 (NOT_2_out, Contador_q);
  Register #(.width(4)) Registro_A (.D(demultiplexer_1_out0), .Q(Registro_A_q), .clk(Contador_q));  // open: en, clr
  Register #(.width(4)) Registro_B (.D(demultiplexer_1_out1), .Q(Registro_B_q), .clk(NOT_2_out));  // open: en, clr
  assign bit_extender_1_out = {{4{1'b0}}, Registro_A_q};  // Bit_Extender bit_extender_1
  assign bit_extender_2_out = {{4{1'b0}}, Registro_B_q};  // Bit_Extender bit_extender_2
  Bit_Extender #(.out_width(4)) bit_extender_3 (.in(bit_extender_1_out), .out(bit_extender_3_out));
  Bit_Extender #(.out_width(4)) bit_extender_4 (.in(bit_extender_2_out), .out(bit_extender_4_out));
  assign not_3_out = ~bit_extender_2_out;  // NOT_Gate not_3, 8 bits wide
  and AND (AND_5_out[3], bit_extender_4_out[3], bit_extender_3_out[3]);
  Adder adder_1 (.a(bit_extender_1_out), .b(not_3_out), .out(adder_1_out), .cin(1'b1));  // open: cout
  and AND_2 (AND_5_out[2], bit_extender_4_out[3], bit_extender_3_out[2]);
  Adder adder_2 (.a(bit_extender_1_out), .b(bit_extender_2_out), .out(adder_2_out));  // open: cin, cout
  Subtractor subtractor_1 (.a(bit_extender_1_out), .b(bit_extender_2_out), .out(subtractor_1_out));  // open: bin, bout
  Divider divider_1 (.a(bit_extender_1_out), .b(bit_extender_2_out), .out(divider_1_out));  // open: upper, rem
  assign OR_out = bit_extender_1_out | bit_extender_2_out;  // OR_Gate OR, 8 bits wide
  assign XOR_out = bit_extender_1_out ^ bit_extender_2_out;  // XOR_Gate XOR, 8 bits wide
  assign AND_3_out = bit_extender_1_out & bit_extender_2_out;  // AND_Gate AND_3, 8 bits wide
  assign NOT_4_out = ~bit_extender_1_out;  // NOT_Gate NOT_4, 8 bits wide
  and AND_4 (AND_5_out[1], bit_extender_4_out[3], bit_extender_3_out[1]);
  and AND_5 (AND_5_out[0], bit_extender_4_out[3], bit_extender_3_out[0]);
  Counter #(.width(4), .max('ha)) Contador_2 (
    .Q(Contador_2_q), .clk(multiplexer_1_out));  // open: load, D, count, carry, clr
  assign bit_extender_5_out = {{3{1'b0}}, multiplexer_1_out};  // Bit_Extender bit_extender_5
  and AND_6 (AND_9_out[3], bit_extender_4_out[2], bit_extender_3_out[3]);
  Subtractor #(.width(4)) subtractor_2 (
    .a(Contador_2_q), .b(bit_extender_5_out), .out(subtractor_2_out));  // open: bin, bout
  not NOT_5 (NOT_5_out, multiplexer_1_out);
  and AND_7 (AND_9_out[2], bit_extender_4_out[2], bit_extender_3_out[2]);
  Multiplexer #(.select(4), .width(8)) multiplexer_2 (
    .in0(bit_extender_1_out), .in1(bit_extender_2_out), .in2(adder_2_out), .in3(subtractor_1_out),
    .in4(AND_17_out), .in5(divider_1_out), .in6(OR_out), .in7(XOR_out), .in8(AND_3_out), .in9(NOT_4_out),
    .in10(adder_1_out), .out(multiplexer_2_out), .sel(rom_1_data));  // open: in11, in12, in13, in14, in15, en
  and AND_8 (AND_9_out[1], bit_extender_4_out[2], bit_extender_3_out[1]);
  assign out_1 = NOT_5_out ? multiplexer_2_out : 8'bz;  // Controlled_Buffer Control_de_Buffer
  and AND_9 (AND_9_out[0], bit_extender_4_out[2], bit_extender_3_out[0]);
  // Probe on rom_1_data
  ROM #(.addrWidth(4), .dataWidth(16)) rom_1 (.addr(subtractor_2_out), .data({rom_1_data_2, rom_1_data}));  // open: sel
  and AND_10 (AND_13_out[3], bit_extender_4_out[1], bit_extender_3_out[3]);
  and AND_11 (AND_13_out[2], bit_extender_4_out[1], bit_extender_3_out[2]);
  and AND_12 (AND_13_out[1], bit_extender_4_out[1], bit_extender_3_out[1]);
  RAM ram_1 (.addr(rom_1_data_2[15:8]), .data(out_1), .clk(multiplexer_1_out), .ld(Not_6_out));  // open: sel, clr
  not Not_6 (Not_6_out, NOT_5_out);
  and AND_13 (AND_13_out[0], bit_extender_4_out[1], bit_extender_3_out[0]);
  and AND_14 (AND_16_out[2], bit_extender_4_out[0], bit_extender_3_out[3]);
  and AND_15 (AND_16_out[1], bit_extender_4_out[0], bit_extender_3_out[2]);
  and AND_16 (AND_16_out[0], bit_extender_4_out[0], bit_extender_3_out[1]);
  Adder #(.width(4)) adder_3 (
    .a({1'b0, AND_16_out}), .b(AND_13_out), .out({adder_3_out[2:0], AND_17_out[1]}), .cin(1'b0),
    .cout(adder_3_out[3]));
  ROM #(.dataWidth(12)) rom_2 (.addr(out_1), .data(rom_2_data));  // open: sel
  _7_Segment_Display u_7_segment_display_1 (
    .g(display_1_g), .f(display_1_f), .a(display_1_a1), .b(display_1_b2), .e(display_1_e), .d(display_1_d2),
    .c(display_1_c2));  // open: dp
  and AND_17 (AND_17_out[0], bit_extender_4_out[0], bit_extender_3_out[0]);
  Adder #(.width(4)) adder_4 (
    .a(adder_3_out), .b(AND_9_out), .out({adder_4_out[2:0], AND_17_out[2]}), .cin(1'b0), .cout(adder_4_out[3]));
  Adder #(.width(4)) adder_5 (.a(adder_4_out), .b(AND_5_out), .out(AND_17_out[6:3]), .cin(1'b0), .cout(AND_17_out[7]));
  display display_1 (
    .a(rom_2_data[11]), .b(rom_2_data[8]), .c(rom_2_data[9]), .d(rom_2_data[10]), .a1(display_1_a1),
    .b2(display_1_b2), .c2(display_1_c2), .d2(display_1_d2), .e(display_1_e), .f(display_1_f), .g(display_1_g));
  _7_Segment_Display u_7_segment_display_2 (
    .g(display_2_g), .f(display_2_f), .a(display_2_a1), .b(display_2_b2), .e(display_2_e), .d(display_2_d2),
    .c(display_2_c2));  // open: dp
  display display_2 (
    .a(rom_2_data[7]), .b(rom_2_data[6]), .c(rom_2_data[5]), .d(rom_2_data[4]), .a1(display_2_a1),
    .b2(display_2_b2), .c2(display_2_c2), .d2(display_2_d2), .e(display_2_e), .f(display_2_f), .g(display_2_g));
  _7_Segment_Display u_7_segment_display_3 (
    .g(display_3_g), .f(display_3_f), .a(display_3_a1), .b(display_3_b2), .e(display_3_e), .d(display_3_d2),
    .c(display_3_c2));  // open: dp
  display display_3 (
    .a(rom_2_data[3]), .b(rom_2_data[2]), .c(rom_2_data[1]), .d(rom_2_data[0]), .a1(display_3_a1),
    .b2(display_3_b2), .c2(display_3_c2), .d2(display_3_d2), .e(display_3_e), .f(display_3_f), .g(display_3_g));

  // Notes on the sheet:
  //   Franklin Leon
  //   Telcado con Push Button
  //   Codificador de Prioridad
  //   Bit Extender
  //   Bit Extender
  //   0000 - Guardar A
  //   0101 - Guardar B
  //   0202 - Suma
  //   0303 - Resta
  //   0404 - Multiplicacion
  //   0505 - Division
  //   0606 - OR
  //   0707 - XOR
  //   0808 - AND
  //   0909 - Not
  //   contents of rom_1 (hex, n*v repeats v):
  //   0 101 202 303 404 505 606 707 808 909 a0a
  //   El que maneja la ram el ultimo
  //   El segundo maneja el opcode
  //   0a0a - Resta de Complemento A2
  //   Cargar Datos Almacenados
  //   RAM
  //   Rom para convertir de binario a decimal
  //   contents of rom_2 (hex, n*v repeats v):
  //   0 1 2 3 4 5 6 7 8 9 10 11 12 13 14 15 16 17 18 19 20 21 22 23 24 25 26 27 28 29 30 31 32 33 34 35 36
  //   37 38 39 40 41 42 43 44 45 46 47 48 49 50 51 52 53 54 55 56 57 58 59 60 61 62 63 64 65 66 67 68 69
  //   70 71 72 73 74 75 76 77 78 79 80 81 82 83 84 85 86 87 88 89 90 91 92 93 94 95 96 97 98 99 100 101
  //   102 103 104 105 106 107 108 109 110 111 112 113 114 115 116 117 118 119 120 121 122 123 124 125 126
  //   127 128 129 130 131 132 133 134 135 136 137 138 139 140 141 142 143 144 145 146 147 148 149 150 151
  //   152 153 154 155 156 157 158 159 160 161 162 163 164 165 166 167 168 169 170 171 172 173 174 175 176
  //   177 178 179 180 181 182 183 184 185 186 187 188 189 190 191 192 193 194 195 196 197 198 199 200 201
  //   202 203 204 205 206 207 208 209 210 211 212 213 214 215 216 217 218 219 220 221 222 223 224 225 226
  //   227 228 229 230 231 232 233 234 235 236 237 238 239 240 241 242 243 244 245 246 247 248 249 250 251
  //   252 253 254 255
endmodule

module display (
  input  a,
  input  b,
  input  c,
  input  d,
  output a1,
  output b2,
  output c2,
  output d2,
  output e,
  output f,
  output g
);

  wire and_1_out, and_2_out, and_3_out, and_4_out, and_5_out, and_6_out, and_7_out, and_8_out, and_9_out,
       and_10_out, and_11_out, and_12_out, and_13_out, and_14_out, and_15_out, and_16_out, and_17_out,
       and_18_out, and_19_out, and_20_out, and_21_out, and_22_out, and_23_out, and_24_out, and_25_out,
       and_26_out, not_1_out, not_2_out, not_3_out, not_4_out, not_5_out, not_6_out, not_7_out, not_8_out,
       not_9_out, not_10_out, not_11_out, not_12_out, not_13_out, not_14_out, not_15_out, not_16_out,
       not_17_out, not_18_out, not_19_out, not_20_out, not_21_out, not_22_out, not_23_out, not_24_out,
       not_25_out, not_26_out, not_27_out, not_28_out, not_29_out, not_30_out, not_31_out, not_32_out,
       not_33_out, not_34_out, not_35_out, not_36_out, not_37_out, not_38_out, not_39_out, not_40_out,
       not_41_out, not_42_out, not_43_out, not_44_out, not_45_out, not_46_out, not_47_out, not_48_out,
       not_49_out, not_50_out, not_51_out, not_52_out;

  not not_1 (not_1_out, a);
  and and_1 (and_1_out, not_1_out, not_2_out, not_3_out);
  not not_2 (not_2_out, b);
  not not_3 (not_3_out, d);
  not not_4 (not_4_out, a);
  and and_2 (and_2_out, not_4_out, c);
  not not_5 (not_5_out, a);
  and and_3 (and_3_out, not_5_out, b, d);
  and and_4 (and_4_out, a, not_6_out, not_7_out);
  not not_6 (not_6_out, b);
  not not_7 (not_7_out, c);
  not not_8 (not_8_out, a);
  and and_5 (and_5_out, not_8_out, not_9_out);
  not not_9 (not_9_out, b);
  not not_10 (not_10_out, a);
  not not_11 (not_11_out, c);
  and and_6 (and_6_out, not_10_out, not_11_out, not_12_out);
  not not_12 (not_12_out, d);
  not not_13 (not_13_out, b);
  and and_7 (and_7_out, not_13_out, not_14_out);
  not not_14 (not_14_out, c);
  not not_15 (not_15_out, a);
  and and_8 (and_8_out, not_15_out, c, d);
  not not_16 (not_16_out, b);
  and and_9 (and_9_out, not_16_out, not_17_out);
  not not_17 (not_17_out, c);
  not not_18 (not_18_out, a);
  and and_10 (and_10_out, not_18_out, d);
  not not_19 (not_19_out, a);
  and and_11 (and_11_out, not_19_out, b);
  not not_20 (not_20_out, a);
  not not_21 (not_21_out, b);
  not not_22 (not_22_out, d);
  not not_23 (not_23_out, a);
  not not_24 (not_24_out, b);
  not not_25 (not_25_out, a);
  not not_26 (not_26_out, d);
  not not_27 (not_27_out, a);
  not not_28 (not_28_out, c);
  not not_29 (not_29_out, b);
  not not_30 (not_30_out, c);
  not not_31 (not_31_out, b);
  not not_32 (not_32_out, c);
  and and_12 (and_12_out, not_31_out, not_32_out, not_33_out);
  not not_33 (not_33_out, d);
  not not_34 (not_34_out, a);
  and and_13 (and_13_out, not_34_out, c, not_35_out);
  not not_35 (not_35_out, d);
  not not_36 (not_36_out, a);
  and and_14 (and_14_out, not_36_out, not_37_out, not_38_out);
  not not_37 (not_37_out, c);
  not not_38 (not_38_out, d);
  not not_39 (not_39_out, a);
  and and_15 (and_15_out, not_39_out, b, not_40_out);
  not not_40 (not_40_out, c);
  not not_41 (not_41_out, a);
  and and_16 (and_16_out, not_41_out, b, not_42_out);
  not not_42 (not_42_out, d);
  not not_43 (not_43_out, b);
  and and_17 (and_17_out, a, not_43_out, not_44_out);
  not not_44 (not_44_out, c);
  not not_45 (not_45_out, a);
  not not_46 (not_46_out, b);
  and and_18 (and_18_out, not_45_out, not_46_out, c);
  not not_47 (not_47_out, a);
  and and_19 (and_19_out, not_47_out, b, not_48_out);
  not not_48 (not_48_out, c);
  not not_49 (not_49_out, a);
  and and_20 (and_20_out, not_49_out, b, not_50_out);
  not not_50 (not_50_out, d);
  and and_21 (and_21_out, a, not_51_out, not_52_out);
  not not_51 (not_51_out, b);
  not not_52 (not_52_out, c);
  or or_1 (a1, and_1_out, and_2_out, and_3_out, and_4_out);
  or or_2 (b2, and_5_out, and_6_out, and_7_out, and_8_out);
  or or_3 (c2, and_9_out, and_10_out, and_11_out);
  and and_22 (and_22_out, not_20_out, not_21_out, not_22_out);
  and and_23 (and_23_out, not_23_out, not_24_out, c);
  and and_24 (and_24_out, not_25_out, c, not_26_out);
  and and_25 (and_25_out, not_27_out, b, not_28_out, d);
  and and_26 (and_26_out, a, not_29_out, not_30_out);
  or or_4 (e, and_12_out, and_13_out);
  or or_5 (f, and_14_out, and_15_out, and_16_out, and_17_out);
  or or_6 (g, and_18_out, and_19_out, and_20_out, and_21_out);
  or or_7 (d2, and_22_out, and_23_out, and_24_out, and_25_out, and_26_out);
endmodule
